# Fritzing sketch thesketch (saved by Fritzing 0.9.3b)

parts:
  Part1 = Arduino Micro (Rev3)
  Part2 = Motor Driver 1A Dual TB6612FNG
  BAT1 = BC9VPC [package=bc9vpc]  # not connected
  M1 = DC Motor
  M2 = DC Motor
  HC-SR04_Sensor_1 = HC-SR04 Ultrasonic Distance Sensor

nets:
  N1: Part1.D5_PWM, HC-SR04_Sensor_1.TRIG
  N2: Part1.D6_PWM/A7, Part2.AIN1
  N3: Part1.D7, Part2.AIN2
  N4: Part1.D8_PWM/A8, HC-SR04_Sensor_1.ECHO
  N5: Part1.D9_PWM/A9, Part2.BIN2
  N6: Part1.D10_PWM/A10, Part2.BIN1
  GND: Part1.GND, HC-SR04_Sensor_1.GND
  5V: Part1.5V, HC-SR04_Sensor_1.VCC
  N7: Part2.B01, M2.pin_1
  N8: Part2.B02, M2.pin_2
  N9: Part2.A02, M1.pin_2
  N10: Part2.A01, M1.pin_1
